# Fritzing sketch Controlling board (saved by Fritzing 0.9.3b)

parts:
  IC1 = IC, DIP package, 28 pins [chip_label=MCP23017]
  J1 = Basic Servo
  R1 = Resistor [tolerance=±5% resistance=10k package=THT]
  U4 = CNZ1120 [package=cnz1120]
  U5 = CNZ1120 [package=cnz1120]
  U6 = CNZ1120 [package=cnz1120]
  U7 = CNZ1120 [package=cnz1120]
  U8 = CNZ1120 [package=cnz1120]
  U9 = CNZ1120 [package=cnz1120]
  U10 = CNZ1120 [package=cnz1120]
  U11 = CNZ1120 [package=cnz1120]
  R2 = Resistor [tolerance=±5% resistance=10k package=THT]
  R3 = Resistor [tolerance=±5% resistance=10k package=THT]
  R4 = Resistor [tolerance=±5% resistance=10k package=THT]
  R5 = Resistor [tolerance=±5% resistance=10k package=THT]
  R6 = Resistor [tolerance=±5% resistance=10k package=THT]
  R7 = Resistor [tolerance=±5% resistance=10k package=THT]
  R8 = Resistor [tolerance=±5% resistance=10k package=THT]
  R9 = Resistor [tolerance=±5% resistance=1k package=THT]
  LED3 = LED - 5mm [color="Red (633nm)" package="5 mm [THT]"]
  R11 = Resistor [tolerance=±5% resistance=220 package=THT]
  LED4 = LED - 5mm [color="Red (633nm)" package="5 mm [THT]"]
  R12 = Resistor [tolerance=±5% resistance=220 package=THT]
  LED5 = LED - 5mm [color="Red (633nm)" package="5 mm [THT]"]
  R13 = Resistor [tolerance=±5% resistance=220 package=THT]
  LED6 = LED - 5mm [color="Red (633nm)" package="5 mm [THT]"]
  R14 = Resistor [tolerance=±5% resistance=220 package=THT]
  LED7 = LED - 5mm [color="Red (633nm)" package="5 mm [THT]"]
  R15 = Resistor [tolerance=±5% resistance=220 package=THT]
  LED8 = LED - 5mm [color="Red (633nm)" package="5 mm [THT]"]
  R16 = Resistor [tolerance=±5% resistance=220 package=THT]
  LED9 = LED - 5mm [color="Red (633nm)" package="5 mm [THT]"]
  R17 = Resistor [tolerance=±5% resistance=220 package=THT]
  LED10 = LED - 5mm [color="Red (633nm)" package="5 mm [THT]"]
  R18 = Resistor [tolerance=±5% resistance=220 package=THT]
  J3 = Basic Servo
  J4 = Basic Servo
  J6 = Basic Servo
  J7 = Basic Servo
  J9 = Screw terminal - 2 pins [package=THT]
  J10 = Screw terminal - 2 pins [package=THT]
  J11 = screw terminal, 5 pins
  R19 = Resistor [tolerance=±5% resistance=220 package=THT]
  R20 = Resistor [tolerance=±5% resistance=220 package=THT]
  R21 = Resistor [tolerance=±5% resistance=220 package=THT]
  R22 = Resistor [tolerance=±5% resistance=220 package=THT]
  R23 = Resistor [tolerance=±5% resistance=220 package=THT]
  R24 = Resistor [tolerance=±5% resistance=220 package=THT]
  R25 = Resistor [tolerance=±5% resistance=220 package=THT]
  R26 = Resistor [tolerance=±5% resistance=220 package=THT]

nets:
  N1: IC1.pin1, R1.Pin_0, U4.4
  N2: IC1.pin2, U5.4, R2.Pin_0
  N3: IC1.pin3, U6.4, R3.Pin_0
  N4: IC1.pin4, U7.4, R4.Pin_0
  N5: IC1.pin5, U8.4, R5.Pin_0
  N6: IC1.pin6, U9.4, R6.Pin_0
  N7: IC1.pin7, U10.4, R7.Pin_0
  N8: IC1.pin8, U11.4, R8.Pin_0
  VCC: IC1.pin9, J1.vcc, U4.3, U5.3, U6.3, U7.3, U8.3, U9.3, U10.3, U11.3, R9.Pin_1, J3.vcc, J4.vcc, J6.vcc, J7.vcc, J9.pin1, R19.Pin_1, R20.Pin_1, R21.Pin_1, R22.Pin_1, R23.Pin_1, R24.Pin_1, R25.Pin_1, R26.Pin_1
  GND: IC1.pin10, IC1.pin15, IC1.pin16, IC1.pin17, J1.gnd, R1.Pin_1, U4.2, U5.2, U6.2, U7.2, U8.2, U9.2, U10.2, U11.2, R2.Pin_1, R3.Pin_1, R4.Pin_1, R5.Pin_1, R6.Pin_1, R7.Pin_1, R8.Pin_1, R11.Pin_0, R12.Pin_0, R13.Pin_0, R14.Pin_0, R15.Pin_0, R16.Pin_0, R17.Pin_0, R18.Pin_0, J3.gnd, J4.gnd, J6.gnd, J7.gnd, J9.pin2
  N9: IC1.pin12, J10.pin2
  N10: IC1.pin13, J10.pin1
  N11: IC1.pin18, R9.Pin_0
  N12: IC1.pin21, LED10.anode
  N13: IC1.pin22, LED9.anode
  N14: IC1.pin23, LED8.anode
  N15: IC1.pin24, LED7.anode
  N16: IC1.pin25, LED6.anode
  N17: IC1.pin26, LED5.anode
  N18: IC1.pin27, LED4.anode
  N19: IC1.pin28, LED3.anode
  N20: J1.pulse, J11.pin2
  N21: U4.1, R19.Pin_0
  N22: U5.1, R20.Pin_0
  N23: U6.1, R21.Pin_0
  N24: U7.1, R22.Pin_0
  N25: U8.1, R23.Pin_0
  N26: U9.1, R24.Pin_0
  N27: U10.1, R25.Pin_0
  N28: U11.1, R26.Pin_0
  N29: LED3.cathode, R11.Pin_1
  N30: LED4.cathode, R12.Pin_1
  N31: LED5.cathode, R13.Pin_1
  N32: LED6.cathode, R14.Pin_1
  N33: LED7.cathode, R15.Pin_1
  N34: LED8.cathode, R16.Pin_1
  N35: LED9.cathode, R17.Pin_1
  N36: LED10.cathode, R18.Pin_1
  N37: J3.pulse, J11.pin3
  N38: J4.pulse, J11.pin4
  N39: J6.pulse, J11.pin5
  N40: J7.pulse, J11.pin1

notes:
  I2C connector
  5V power connector
  Servo control signals connector
